# Fritzing sketch IoTCircuitoEditable (saved by Fritzing 0.9.10b)
breadboards: 2

parts:
  Componente1 = FC-28 Soil Hygrometer Module - Probe
  Componente2 = FC-28 Soil Hygrometer Module
  Componente3 = LCD1602-I2C
  WATER_PUMP1 = water pump/motor
  LED1 = RGB LED (com. cathode, rgb) [package="5 mm [THT]"]
  LED3 = smd LED [color="Red (633nm)" package="0805 [SMD]"]
  U1 = ESP32-38PinWide [part_number=ESP32-38PinWide]
  A1 = DHT22 module
  LED4 = LEDs [package=led10mm]
  RY1 = KF-301 Relay [package=THT]
  HC-SR04_Sensor_1 = HC-SR04 Ultrasonic Distance Sensor
  R1 = Resistor [tolerance=±5% resistance=220 package="0402 [SMD]"]
  R2 = Resistor [tolerance=±5% resistance=220 package="0402 [SMD]"]
  R3 = Resistor [tolerance=±5% power=0.25 resistance=220 package=THT]
  R4 = Resistor [tolerance=±5% power=0.25 resistance=220 package=THT]
  R5 = Resistor [tolerance=±5% power=0.25 resistance=220 package=THT]

nets:
  N1: Componente1.POS, Componente2.POS
  N2: Componente1.NEG, Componente2.NEG
  VCC: Componente2.VCC, WATER_PUMP1.pin_2, U1.3.3, A1.+, RY1.power, HC-SR04_Sensor_1.VCC
  GND: Componente2.GND, Componente3.GND, LED1.common_cathode, LED3.cathode, U1.GND, A1.-, LED4.A, RY1.ground, RY1.C, HC-SR04_Sensor_1.GND
  N3: Componente2.AO, U1.GPIO35
  VCC_2: Componente3.VCC, U1.VIN
  N4: Componente3.SDA, U1.GPIO21
  N5: Componente3.SCL, U1.GPIO22
  N6: WATER_PUMP1.pin_1, RY1.NO
  N7: LED1.red_anode, R5.Pin_1
  N8: LED1.green_anode, R3.Pin_1
  N9: LED1.blue_anode, R4.Pin_1
  N10: LED3.anode, R1.Pin_0
  N11: U1.GPIO33, R2.Pin_1
  N12: U1.GPIO14, HC-SR04_Sensor_1.ECHO
  N13: U1.GPIO12, HC-SR04_Sensor_1.TRIG
  N14: U1.GPIO13, R1.Pin_1
  N15: U1.GPIO15, RY1.signal
  N16: U1.GPIO16, A1.Out
  N17: U1.GPIO17, R5.Pin_0
  N18: U1.GPIO5, R4.Pin_0
  N19: U1.GPIO18, R3.Pin_0
  N20: LED4.C, R2.Pin_0

notes:
  SENSOR DHT22
  +: conectado al positivo del protoboard
  OUT: conectado al pin G16
  -: conectado al negativo del protoboard
  SENSOR HC-SR04
  - Vcc: conectado al positivo del protoboard
  - Trig: conectado al pin G12
  - Echo: conectado al pin G14
  - Gnd: conectado al negativo del protoboard
  LED MULTICOLOR
  - Conectado al negativo de protoboard
  - Conectado al pin G33
  MÓDULO DEL FC-28
  (Se usa de manera analógica)
  - VCC: Conectado al positivo del protoboard
  - GND: Conectado al negativo del protoboard
  - AO: Conectado al pin G35
  SENSOR FC-28
  - Se conecta al VCC y al GND de su módulo
  LED RGB
  - Ánodo rojo: conectado al pin G17
  - Ánodo verde: conectado al pin G18
  - Ánodo azul: conectado al pin G5
  - Cátodo común: conectado al pin G17
  LCD I2C 16x2
  - GND: conectado al negativo del protoboard
  - VCC: conectado al positivo del protoboard
  - SDA: conectado al pin G21
  - SCL: conectado al pin G22
  RELE
  - VCC: conectado al positivo del protoboard
  - GND: conectado al negativo del protoboard
  - IN: conectado al pin G15
  BOMBA DE AGUA
  - Negativo: conectado al NO del rele
  - Positivo: conectado al positivo del protoboard
  LED ROJO
  - Ánodo:
  conectado al pin G13
  - Cátodo: conectado al ladonegativo del protoboard

custom parts:
  FC-28 Soil Hygrometer Module - Probe: The FC-28 is a soil hygrometer module that uses the Texas Instruments LM393 comparator chip to provide an analog measurement of soil humidity.
  FC-28 Soil Hygrometer Module: The FC-28 is a soil hygrometer module that uses the Texas Instruments LM393 comparator chip to provide an analog measurement of soil humidity. The digital output is high when soil moisture is over a certain threshold, as determined by adjusting the potentiometer.
  LCD1602-I2C: A standard character display, usually with 2x16 characters. Comes in many colors with LCM1602 IIC attached.
  water pump/motor: WATER PUMP BY ARDUBLOCKTR
  ESP32-38PinWide: Generic 38-Pin ESP32 with wide format (only access to one side of pins on a breadboard) based on Stephen Lilley's HiLetgo ESP-WROOM-32 ESP32 ESP-32S Development Board.
  DHT22 module: DHT22 module. Pins VCC Data GND.
  KF-301 Relay: KF-301 SPDT Relay module using SRD-05VDC-SL-C relay.
